# Fritzing sketch d1mini_perfboard (saved by Fritzing 1.0.5)
perfboards: 2

parts:
  M1 = cc1101 module
  A1 = Az-delivery ESP32 D1-Mini Nodemcu

nets:
  N1: M1.pin_1, M1.pin_2, A1.Pin_28
  N2: M1.pin_3, A1.Pin_26
  N3: M1.pin_4, A1.Pin_24
  N4: M1.pin_5, A1.Pin_25
  N5: M1.pin_6, A1.Pin_15
  N6: M1.pin_7, A1.Pin_27
  N7: M1.pin_8, A1.Pin_17
  N8: M1.pin_9, M1.pin_10, A1.Pin_10, A1.Pin_14

custom parts:
  cc1101 module: CC1101 rf module.
  Az-delivery ESP32 D1-Mini Nodemcu: ESP32 D1 Mini Nodemcu WiFi Module + Bluetooth Internet Development Board.
