# Fritzing sketch hardware_diagram (saved by Fritzing 1.0.5)

parts:
  M1 = DOIT Esp32 DevKit v1 (30 pins long, 11 pins width) [part_number=ESP32S-PIN30]
  M2 = cc1101 module

nets:
  N1: M1.3V3, M2.pin_1, M2.pin_2
  N2: M1.GND, M2.pin_9, M2.pin_10
  N3: M1.D2, M2.pin_8
  N4: M1.D4, M2.pin_6
  N5: M1.D5, M2.pin_7
  N6: M1.D18, M2.pin_4
  N7: M1.D19, M2.pin_5
  N8: M1.D23, M2.pin_3

custom parts:
  DOIT Esp32 DevKit v1 (30 pins long, 11 pins width): The DOIT Esp32 DevKit v1 is one of the development board created by DOIT to evaluate the ESP-WROOM-32 module. It is based on the ESP32 microcontroller that boasts Wifi, Bluetooth, Ethernet and Low Power support all in a single chip. (vanepp) made breadboard work, adjusted pin numbering and labels and reduced size of schematic and cleaned up pcb. This chip is 30pins long (2 x15) and 11 pins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
  cc1101 module: CC1101 rf module.
